# Fritzing sketch proyecto (saved by Fritzing 0.9.3b)

parts:
  Componente2 = Arduino Mega 2560 (Rev3)
  S1 = Momentary Switch [package=ksa_sealed_tac_switch]
  S2 = Momentary Switch [package=ksa_sealed_tac_switch]
  S3 = Momentary Switch [package=ksa_sealed_tac_switch]
  S4 = Momentary Switch [package=ksa_sealed_tac_switch]
  S5 = Pushbutton [package=THT]
  S6 = Pushbutton [package=THT]
  S7 = Pushbutton [package=THT]
  U1 = RELAY [package=relay-g5q]
  U2 = RELAY [package=relay-g5q]
  U3 = RELAY [package=relay-g5q]
  S8 = Pushbutton [package=THT]
  S9 = Pushbutton [package="[THT]"]
  S10 = Pushbutton [package=THT]
  S11 = Pushbutton [package=THT]
  Componente3 = Rotoshield - Motor driver shield for Arduino
  M1 = DC Motor
  S12 = Pushbutton [package=THT]
  RHT1 = Humidity and Temperature Sensor RHT03
  LCD1 = LCD screen
  S13 = Pushbutton [package=THT]
  S14 = Pushbutton [package=THT]
  S16 = Pushbutton [package=THT]
  S17 = Pushbutton [package=THT]
  S18 = Pushbutton [package=THT]
  S19 = Pushbutton [package=THT]
  S20 = Pushbutton [package=THT]
  S21 = Pushbutton [package=THT]
  R1 = Rotary Potentiometer (Small) [maximum_resistance=100kΩ package=THT]
  R2 = Resistor [tolerance=±5% resistance=220 package="1206 [SMD]"]

nets:
  N1: Componente2.D12_PWM, S5.leg1
  N2: Componente2.D11_PWM, S6.leg1
  N3: Componente2.D9_PWM, RHT1.Data-signal
  N4: Componente2.D8_PWM, S7.leg1
  5V: Componente2.5V, S1.4, S2.4, S3.4, S4.4, S5.leg0, S6.leg0, S7.leg0, U1.COIL2, U1.MAIN, U2.COIL2, U3.COIL2, RHT1.Vcc
  GND: Componente2.GND, U1.COIL1, U2.COIL1, U3.COIL1, S11.leg0, Componente3.GND, M1.pin_1, S12.leg1, RHT1.GND_2
  N5: Componente2.D2_PWM, S1.1
  N6: Componente2.D5_PWM, S3.1
  N7: Componente2.D6_PWM, S2.1
  N8: Componente2.D25, S4.1
  N9: Componente2.D44, Componente3.M2-2
  N10: Componente2.D53, Componente3.M2-1
  N11: U1.NC, S11.leg1
  N12: U2.MAIN, U3.MAIN, S8.leg0
  N13: U2.NC, S9.Pin_1, S9.Pin_2
  N14: U3.NC, S10.leg0
  N15: S8.leg1, S9.Pin_3, S9.Pin_4, S10.leg1
  N16: Componente3.VIN, S12.leg0
  N17: Componente3.VCC, M1.pin_2
  N18: LCD1.VSS, LCD1.LED-, S13.leg1
  N19: LCD1.VDD, S14.leg0, R2.Pin_1
  N20: LCD1.V0, R1.wiper
  N21: LCD1.RS, S16.leg1
  N22: LCD1.E, S17.leg1
  N23: LCD1.DB4, S18.leg1
  N24: LCD1.DB5, S20.leg1
  N25: LCD1.DB6, S19.leg1
  N26: LCD1.DB7, S21.leg1
  N27: LCD1.LED+, R2.Pin_0

notes:
  AC POWER SUPPLY
  REGLETA
  BOMBILLA
  Ventilador
  Pulsador Bombilla
  Pulsadores Persiana
  Pulsador REGLETA
  Puente H
  Controlador Motor DC (persiana)
  Fuente Al. Motor
  Sensor de temperatura y humedad
  gnd
  5v cc
  33
  34
  35
  36
  39
  40
  FINALES DE CARRERA
